// Logisim project Introduction.circ as structural Verilog: 8 circuits, main circuit implication
module implication (
  input  x,
  input  y,
  output z,
  output out_4
);

  wire not_1_out;

  not not_1 (not_1_out, x);
  or or_1 (out_4, not_1_out, y);

  assign z = out_4;
endmodule

module parity (
  input  x,
  input  y,
  output z,
  output out_4
);

  wire and_1_out, and_2_out, not_1_out, not_2_out;

  not not_1 (not_1_out, x);
  not not_2 (not_2_out, y);
  and and_1 (and_1_out, not_1_out, y);
  and and_2 (and_2_out, x, not_2_out);
  or or_1 (out_4, and_1_out, and_2_out);

  assign z = out_4;
endmodule

module equivalence (
  input  x,
  input  y,
  output z,
  output out_4
);

  wire parity_1_z;

  parity parity_1 (.x(x), .z(parity_1_z), .y(y));  // open: out_4
  not not_1 (out_4, parity_1_z);

  assign z = out_4;
endmodule

module tautology (
  input  x,
  input  y,
  output out_3,
  output z
);

  wire parity_1_z, xor_1_out;

  parity parity_1 (.x(x), .z(parity_1_z), .y(y));  // open: out_4
  xor xor_1 (xor_1_out, x, y);
  equivalence equivalence_1 (.x(parity_1_z), .z(out_3), .y(xor_1_out));  // open: out_4

  assign z = out_3;
endmodule

module ztand (
  input  [7:0] x,
  output y
);

  wire and_1_out, and_2_out, and_3_out, and_5_out, and_6_out, and_7_out, not_1_out, not_2_out, not_3_out,
       not_4_out, not_5_out, not_6_out, not_7_out, not_8_out;

  not not_1 (not_1_out, x[6]);
  not not_2 (not_2_out, x[7]);
  and and_1 (and_1_out, not_2_out, not_1_out);
  not not_3 (not_3_out, x[5]);
  and and_2 (and_2_out, not_3_out, not_4_out);
  and and_3 (and_3_out, and_1_out, and_2_out);
  not not_4 (not_4_out, x[4]);
  and and_4 (y, and_3_out, and_7_out);
  not not_5 (not_5_out, x[2]);
  not not_6 (not_6_out, x[3]);
  and and_5 (and_5_out, not_6_out, not_5_out);
  not not_7 (not_7_out, x[1]);
  not not_8 (not_8_out, x[0]);
  and and_6 (and_6_out, not_7_out, not_8_out);
  and and_7 (and_7_out, and_5_out, and_6_out);
endmodule

module ztor (
  input  [7:0] x,
  output y
);

  wire or_1_out, or_2_out, or_3_out, or_4_out, or_5_out, or_6_out, or_7_out;

  or or_1 (or_1_out, x[7], x[6]);
  or or_2 (or_2_out, or_1_out, or_3_out);
  or or_3 (or_3_out, x[5], x[4]);
  or or_4 (or_4_out, or_2_out, or_6_out);
  not not_1 (y, or_4_out);
  or or_5 (or_5_out, x[3], x[2]);
  or or_6 (or_6_out, or_5_out, or_7_out);
  or or_7 (or_7_out, x[1], x[0]);
endmodule

module pf4 (
  input  [3:0] x,
  output [3:0] y
);

  wire b1, parity_1_z, parity_2_z;

  and and_1 (y[0], x[0], b1);
  and and_2 (y[1], x[1], b1);
  parity parity_1 (.x(x[0]), .z(parity_1_z), .y(x[1]));  // open: out_4
  parity parity_2 (.x(x[2]), .z(parity_2_z), .y(x[3]));  // open: out_4
  and and_3 (y[2], x[2], b1);
  and and_4 (y[3], x[3], b1);
  parity parity_3 (.x(parity_1_z), .z(b1), .y(parity_2_z));  // open: out_4

  // Other names for the same wires on the sheet: a1 = x[0]; a2 = x[1]; a3 = x[2]; a4 = x[3]; c1 = y[0]; c2 = y[1];
  //   c3 = y[2]; c4 = y[3]
endmodule

module CMOS_NAND (
  input  x,
  input  y,
  output z
);

  wire transistor_3_out;

  Transistor transistor_1 (.in(1'b1), .out(z), .gate(x));
  Transistor #(.\type ("n")) transistor_2 (.in(transistor_3_out), .out(z), .gate(x));
  Transistor #(.\type ("n")) transistor_3 (.in(1'b0), .out(transistor_3_out), .gate(y));
  Transistor transistor_4 (.in(1'b1), .out(z), .gate(y));
endmodule
