// Logisim project Project 1 - Template.circ as structural Verilog: 8 circuits, main circuit implication
module implication (
  input  x,
  input  y,
  output z
);
endmodule

module parity (
  input  x,
  input  y,
  output z
);
endmodule

module equivalence (
  input  x,
  input  y,
  output z
);
endmodule

module tautology (
  input  x,
  input  y,
  output z
);
endmodule

module ztand (
  input  [7:0] x,
  output y
);
endmodule

module ztor (
  input  [7:0] x,
  output y
);
endmodule

module pf4 (
  input  [3:0] x,
  output [3:0] y
);
endmodule

module CMOS_NAND (
  input  x,
  input  y,
  output z
);
endmodule
