// Logisim project Priority Encoder.circ as structural Verilog: 7 circuits, main circuit penc(4)
module penc_4 (
  input  [15:0] y,
  output valid,
  output [3:0] x
);

  wire vr;
  wire [2:0] xl, xr;

  penc_3 penc_3__Right (.in_1(y[7:0]), .x(xr), .v(vr));
  penc_3 penc_3__Left (.in_1(y[15:8]), .x(xl), .v(x[3]));
  or or_1 (valid, vr, x[3]);
  MUX3 MUX3 (.d_0(xr), .s(x[3]), .d_1(xl), .out_4(x[2:0]));

  // Other names for the same wires on the sheet: a_0 = y[0]; a_1 = y[1]; a_2 = y[2]; a_3 = y[3]; a_4 = y[4];
  //   a_5 = y[5]; a_6 = y[6]; a_7 = y[7]; a_8 = y[8]; a_9 = y[9]; a_10 = y[10]; a_11 = y[11]; a_12 = y[12];
  //   a_13 = y[13]; a_14 = y[14]; a_15 = y[15]; x_0_2[2:0] = x[2:0]; vl = x[3]
endmodule

module penc_1 (
  input  [1:0] y,
  output v,
  output x
);

  wire not_1_out;

  not not_1 (not_1_out, y[0]);
  or or_1 (v, y[0], y[1]);
  or or_2 (x, y[1], not_1_out);

  // Other names for the same wires on the sheet: a0 = y[0]; a1 = y[1]
endmodule

module penc_2 (
  input  [3:0] in_1,
  output v,
  output [1:0] x
);

  wire vr, xl, xr;

  or or_1 (v, vr, x[1]);
  MUX1 MUX1 (.d_0(xr), .s(x[1]), .d_1(xl), .r(x[0]));
  penc_1 penc_1__Right (.y(in_1[1:0]), .v(vr), .x(xr));
  penc_1 penc_1__Left (.y(in_1[3:2]), .v(x[1]), .x(xl));

  // Other names for the same wires on the sheet: a0 = in_1[0]; a1 = in_1[1]; a2 = in_1[2]; a3 = in_1[3]; vl = x[1]
endmodule

module MUX1 (
  input  d_0,
  input  s,
  input  d_1,
  output r
);

  wire and_1_out, and_2_out, not_1_out;

  not not_1 (not_1_out, s);
  and and_1 (and_1_out, d_0, not_1_out);
  and and_2 (and_2_out, s, d_1);
  or or_1 (r, and_1_out, and_2_out);
endmodule

module penc_3 (
  input  [7:0] in_1,
  output [2:0] x,
  output v
);

  wire vr;
  wire [1:0] xl, xr;

  or or_1 (v, vr, x[2]);
  MUX2 MUX2 (.d_0(xr), .s(x[2]), .d_1(xl), .out_4(x[1:0]));
  penc_2 Penc_2___Right (.in_1(in_1[3:0]), .v(vr), .x(xr));
  penc_2 Penc_2___Left (.in_1(in_1[7:4]), .v(x[2]), .x(xl));

  // Other names for the same wires on the sheet: a_0 = in_1[0]; a_1 = in_1[1]; a_2 = in_1[2]; a_3 = in_1[3];
  //   a_4 = in_1[4]; a_5 = in_1[5]; a_6 = in_1[6]; a_7 = in_1[7]; x_0_1[1:0] = x[1:0]; vl = x[2]
endmodule

module MUX2 (
  input  [1:0] d_0,
  input  s,
  input  [1:0] d_1,
  output [1:0] out_4
);

  wire and_1_out, and_2_out, and_3_out, and_4_out, not_1_out;

  not not_1 (not_1_out, s);
  and and_1 (and_1_out, d_0[0], not_1_out);
  and and_2 (and_2_out, d_0[1], not_1_out);
  and and_3 (and_3_out, s, d_1[0]);
  and and_4 (and_4_out, s, d_1[1]);
  or or_1 (out_4[0], and_1_out, and_3_out);
  or or_2 (out_4[1], and_2_out, and_4_out);
endmodule

module MUX3 (
  input  [2:0] d_0,
  input  s,
  input  [2:0] d_1,
  output [2:0] out_4
);

  wire _0_2_out, _0_out, _1_2_out, _1_out, _2_2_out, _2_out, not_1_out;

  not not_1 (not_1_out, s);
  and _0 (_0_out, d_0[0], not_1_out);
  and _1 (_1_out, d_0[1], not_1_out);
  and _2 (_2_out, d_0[2], not_1_out);
  and _0_2 (_0_2_out, s, d_1[0]);
  and _1_2 (_1_2_out, s, d_1[1]);
  and _2_2 (_2_2_out, s, d_1[2]);
  or _0_3 (out_4[0], _0_out, _0_2_out);
  or _1_3 (out_4[1], _1_out, _1_2_out);
  or _2_3 (out_4[2], _2_out, _2_2_out);
endmodule
