// Logisim project Variable Length Adder.circ as structural Verilog: 5 circuits, main circuit VarLenAdder
module VarLenAdder (
  input  [3:0] A,
  input  [3:0] B,
  input  [1:0] C,
  output [3:0] S,
  output D,
  output E
);

  wire D1, D2, E1, E2, not_1_out, Selector;
  wire [3:0] Option_0, Option_1;

  not not_1 (not_1_out, C[0]);
  Add1 add1_1 (.a(A[0]), .b(B[0]), .s(Option_0[0]), .c_out(D1));
  and and_1 (Selector, not_1_out, C[1]);
  Multiplexer #(.width(6), .enable("false")) multiplexer_1 (
    .in0({E1, D1, Option_0}), .in1({E2, D2, Option_1}), .out({E, D, S}), .sel(Selector));
  add3 add3_1 (.a(A[3:1]), .b(B[3:1]), .s(Option_0[3:1]), .carry_out(E1));
  add2 add2_1 (.a(A[1:0]), .b(B[1:0]), .s(Option_1[1:0]), .c_out(D2));
  add2 add2_2 (.a(A[3:2]), .b(B[3:2]), .s(Option_1[3:2]), .c_out(E2));

  // Other names for the same wires on the sheet: S_0 = Option_0[0]; S_3_1[2:0] = Option_0[3:1];
  //   Option_0[5:4] = {E1, D1}; S_1_0[1:0] = Option_1[1:0]; S_3_2[1:0] = Option_1[3:2]; Option_1[5:4] = {E2, D2};
  //   P[1:0] = C
endmodule

// add1
module Add1 (
  input  a,
  input  b,
  output s,
  output c_out
);

  and and_1 (c_out, a, b);
  xor xor_1 (s, a, b);
endmodule

module add2 (
  input  [1:0] a,
  input  [1:0] b,
  output [1:0] s,
  output c_out
);

  wire add1_1_c_out;

  Add1 add1_1 (.a(a[0]), .b(b[0]), .s(s[0]), .c_out(add1_1_c_out));
  Add1_half add1_half_1 (.a(a[1]), .b(b[1]), .c_in(add1_1_c_out), .s(s[1]), .c_out(c_out));
endmodule

module Add1_half (
  input  a,
  input  b,
  input  c_in,
  output s,
  output c_out
);

  wire and_1_out, and_2_out, xor_1_out;

  and and_1 (and_1_out, a, b);
  xor xor_1 (xor_1_out, a, b);
  xor xor_2 (s, xor_1_out, c_in);
  and and_2 (and_2_out, c_in, xor_1_out);
  or or_1 (c_out, and_2_out, and_1_out);
endmodule

module add3 (
  input  [2:0] a,
  input  [2:0] b,
  output [2:0] s,
  output carry_out
);

  wire add2_1_c_out;

  add2 add2_1 (.a(a[1:0]), .b(b[1:0]), .s(s[1:0]), .c_out(add2_1_c_out));
  Add1_half add1_half_1 (.a(a[2]), .b(b[2]), .c_in(add2_1_c_out), .s(s[2]), .c_out(carry_out));
endmodule
