// Logisim project template_varlenadder.circ as structural Verilog: 1 circuit, main circuit VarLenAdder
module VarLenAdder (
  input  [3:0] A,
  input  [3:0] B,
  input  [1:0] C,
  output [3:0] S,
  output D,
  output E
);


  // Other names for the same wires on the sheet: P[1:0] = C
endmodule
