// Logisim project Stack.circ as structural Verilog: 1 circuit, main circuit Stack
module Stack (
  input  [2:0] Din,
  input  CLK,
  input  pop,
  input  push,
  input  in_5,
  input  [3:0] in_6,
  output [2:0] Dout,
  output empty,
  output full,
  output [2:0] out_10,
  output [2:0] out_11
);

  wire and_1_out, and_2_out, and_3_out, CE, FF1_control, FF2_control, FF3_control, not_2_out, not_3_out,
       not_4_out, not_5_out, or_1_out, Selector;
  wire [3:0] multiplexer_1_out, multiplexer_2_out, multiplexer_3_out;

  or or_1 (or_1_out, pop, push);
  not not_1 (Selector, push);
  and and_1 (and_1_out, full, push);
  not not_2 (not_2_out, and_1_out);
  and and_2 (and_2_out, FF1_control, FF2_control);
  not not_3 (not_3_out, FF1_control);
  and and_3 (and_3_out, not_3_out, not_4_out);
  not not_4 (not_4_out, FF2_control);
  not not_5 (not_5_out, FF3_control);
  and and_4 (CE, or_1_out, not_2_out);
  and and_5 (full, and_2_out, FF3_control);
  and and_6 (empty, and_3_out, not_5_out);
  Multiplexer #(.width(4), .enable("false")) multiplexer_1 (
    .in0({in_5, Din}), .in1({FF2_control, out_10}), .out(multiplexer_1_out), .sel(Selector));
  Register #(.width(4)) register_1 (.D(multiplexer_1_out), .en(CE), .Q({FF1_control, Dout}), .clk(CLK));  // open: clr
  Multiplexer #(.width(4), .enable("false")) multiplexer_2 (
    .in0({FF1_control, Dout}), .in1({FF3_control, out_11}), .out(multiplexer_2_out), .sel(Selector));
  Register #(.width(4)) register_2 (.D(multiplexer_2_out), .en(CE), .Q({FF2_control, out_10}), .clk(CLK));  // open: clr
  Multiplexer #(.width(4), .enable("false")) multiplexer_3 (
    .in0({FF2_control, out_10}), .in1(in_6), .out(multiplexer_3_out), .sel(Selector));
  Register #(.width(4)) register_3 (.D(multiplexer_3_out), .en(CE), .Q({FF3_control, out_11}), .clk(CLK));  // open: clr

  // Other names for the same wires on the sheet: FF2_Out[3:0] = {FF2_control, out_10};
  //   FF3_Out[3:0] = {FF3_control, out_11}
endmodule
