// Logisim project template_stack.circ as structural Verilog: 1 circuit, main circuit Stack
module Stack (
  input  [2:0] Din,
  input  CLK,
  input  pop,
  input  push,
  output [2:0] Dout,
  output empty,
  output full
);
endmodule
