// Logisim project Game.circ as structural Verilog: 3 circuits, main circuit game
module game (
  input  [1:0] X,
  input  clk,
  input  reset,
  output [1:0] Y
);

  wire [1:0] NS, register_1_q, S;

  Cdelta cdelta_1 (.X(X), .S(S), .NS(NS));
  Register #(.width(2)) register_1 (.D(NS), .en(1'b1), .Q(register_1_q), .clk(clk));  // open: clr
  Clambda clambda_1 (.X(X), .S(S), .Y(Y));  // open: selector
  Multiplexer #(.width(2), .enable("false")) multiplexer_1 (.in0(register_1_q), .in1(2'b00), .out(S), .sel(reset));

  // Notes on the sheet:
  //   Initial state encoding:
  //   Reset Mechanism
endmodule

module Cdelta (
  input  [1:0] X,
  input  [1:0] S,
  output [1:0] NS
);

  wire and_1_out, and_2_out, and_3_out, and_4_out, Indicator1, Indicator2, Indicator3, not_5_out, not_6_out,
       not_7_out, not_8_out, not_9_out, not_10_out, notS0, notS1, notX0, notX1, or_1_out, or_2_out,
       Selector0, Selector1, xnor_1_out, xor_1_out, xor_2_out;
  wire [1:0] multiplexer_1_out;

  not not_1 (notX1, X[1]);
  not not_2 (notX0, X[0]);
  not not_3 (notS1, S[1]);
  not not_4 (notS0, S[0]);
  not not_5 (not_5_out, X[1]);
  not not_6 (not_6_out, X[0]);
  not not_7 (not_7_out, S[1]);
  not not_8 (not_8_out, S[0]);
  not not_9 (not_9_out, S[1]);
  not not_10 (not_10_out, S[0]);
  xor xor_1 (xor_1_out, X[1], X[0]);
  xor xor_2 (xor_2_out, S[1], S[0]);
  and and_1 (and_1_out, not_5_out, not_6_out);
  and and_2 (and_2_out, not_7_out, not_8_out);
  or or_1 (or_1_out, Indicator1, Indicator2);
  and and_3 (and_3_out, X[1], X[0]);
  and and_4 (and_4_out, not_9_out, not_10_out);
  xnor xnor_1 (xnor_1_out, X[1], X[0]);
  and and_5 (Indicator1, xor_1_out, xor_2_out);
  and and_6 (Indicator3, and_1_out, and_2_out);
  or or_2 (or_2_out, or_1_out, Indicator3);
  and and_7 (Indicator2, and_3_out, and_4_out);
  or or_3 (Selector1, xnor_1_out, 1'b0);
  or or_4 (Selector0, or_2_out, 1'b0);
  Multiplexer #(.width(2), .enable("false")) multiplexer_1 (.in0(X), .in1(S), .out(multiplexer_1_out), .sel(Selector1));
  Multiplexer #(.width(2), .enable("false")) multiplexer_2 (
    .in0(multiplexer_1_out), .in1(2'b00), .out(NS), .sel(Selector0));

  // Other names for the same wires on the sheet: S_t[1:0] = S; X_t[1:0] = X
endmodule

module Clambda (
  input  [1:0] X,
  input  [1:0] S,
  output [1:0] Y,
  output selector
);

  wire notX0, notX1, xnor_1_out, xnor_2_out;

  not not_1 (notX1, X[1]);
  not not_2 (notX0, X[0]);
  xnor xnor_1 (xnor_1_out, S[0], X[0]);
  xnor xnor_2 (xnor_2_out, S[1], X[1]);
  and and_1 (selector, xnor_1_out, xnor_2_out);
  Multiplexer #(.width(2), .enable("false")) multiplexer_1 (.in0(2'b00), .in1(X), .out(Y), .sel(selector));
endmodule
