// Logisim project template_game.circ as structural Verilog: 3 circuits, main circuit game
module game (
  input  [1:0] X,
  input  clk,
  input  reset,
  output [1:0] Y
);

  wire [1:0] NS, register_1_q, S;

  Register #(.width(2)) register_1 (.D(NS), .en(1'b1), .Q(register_1_q), .clk(clk));  // open: clr
  Multiplexer #(.width(2), .enable("false")) multiplexer_1 (.in0(register_1_q), .in1(2'b00), .out(S), .sel(reset));

  // Notes on the sheet:
  //   Initial state encoding:
  //   Reset Mechanism
endmodule

module Cdelta (
  input  [1:0] X,
  input  [1:0] S,
  output [1:0] NS
);

  wire notS0, notS1, notX0, notX1;

  not not_1 (notX1, X[1]);
  not not_2 (notX0, X[0]);
  not not_3 (notS1, S[1]);
  not not_4 (notS0, S[0]);
endmodule

module Clambda (
  input  [1:0] X,
  input  [1:0] S,
  output [1:0] Y
);

  wire notX0, notX1;

  not not_1 (notX1, X[1]);
  not not_2 (notX0, X[0]);
endmodule
